// Logisim project alu.circ as structural Verilog: 2 circuits, main circuit main
module main (
  input  [7:0] in_1,
  input  ENABLE,
  input  CLOCK,
  input  [1:0] FS,
  output [7:0] out_5
);

  wire and_1_out, and_2_out, and_3_out, and_4_out, and_5_out, and_6_out, multiplexer_1_out,
       multiplexer_2_out, multiplexer_3_out, multiplexer_4_out, multiplexer_5_out, multiplexer_6_out,
       multiplexer_7_out, multiplexer_8_out, nor_1_out, nor_2_out, nor_3_out, nor_4_out, nor_5_out,
       nor_6_out, not_1_out, not_2_out, xor_1_out, xor_2_out, xor_3_out, xor_4_out, xor_5_out, xor_6_out,
       xor_7_out, xor_8_out, xor_9_out, xor_10_out, xor_11_out, xor_12_out, xor_13_out, xor_14_out;

  Hex_Digit_Display hex_digit_display_1 (.value(in_1[7:4]));  // open: dp
  Hex_Digit_Display hex_digit_display_2 (.value(in_1[3:0]));  // open: dp
  xor xor_1 (xor_1_out, out_5[0], out_5[1]);
  not not_1 (not_1_out, out_5[0]);
  xor xor_2 (xor_2_out, not_1_out, out_5[1]);
  and and_1 (and_1_out, out_5[0], out_5[1]);
  nor nor_1 (nor_1_out, out_5[0], out_5[1]);
  and and_2 (and_2_out, out_5[0], out_5[2], out_5[1]);
  nor nor_2 (nor_2_out, out_5[0], out_5[2], out_5[1]);
  and and_3 (and_3_out, out_5[0], out_5[1], out_5[2], out_5[3]);
  nor nor_3 (nor_3_out, out_5[0], out_5[1], out_5[2], out_5[3]);
  and and_4 (and_4_out, out_5[0], out_5[1], out_5[2], out_5[3], out_5[4]);
  nor nor_4 (nor_4_out, out_5[3], out_5[0], out_5[1], out_5[2], out_5[4]);
  and and_5 (and_5_out, out_5[0], out_5[1], out_5[2], out_5[3], out_5[4], out_5[5]);
  nor nor_5 (nor_5_out, out_5[0], out_5[1], out_5[2], out_5[3], out_5[4], out_5[5]);
  and and_6 (and_6_out, out_5[0], out_5[1], out_5[2], out_5[6], out_5[3], out_5[4], out_5[5]);
  nor nor_6 (nor_6_out, out_5[0], out_5[1], out_5[2], out_5[6], out_5[3], out_5[4], out_5[5]);
  xor xor_3 (xor_3_out, and_1_out, out_5[2]);
  xor xor_4 (xor_4_out, nor_1_out, out_5[2]);
  xor xor_5 (xor_5_out, and_2_out, out_5[3]);
  xor xor_6 (xor_6_out, nor_2_out, out_5[3]);
  xor xor_7 (xor_7_out, and_3_out, out_5[4]);
  xor xor_8 (xor_8_out, nor_3_out, out_5[4]);
  xor xor_9 (xor_9_out, and_4_out, out_5[5]);
  xor xor_10 (xor_10_out, nor_4_out, out_5[5]);
  xor xor_11 (xor_11_out, and_5_out, out_5[6]);
  xor xor_12 (xor_12_out, nor_5_out, out_5[6]);
  xor xor_13 (xor_13_out, and_6_out, out_5[7]);
  xor xor_14 (xor_14_out, nor_6_out, out_5[7]);
  not not_2 (not_2_out, out_5[0]);
  Multiplexer #(.select(2)) multiplexer_1 (
    .in0(1'b0), .in1(in_1[0]), .in2(not_2_out), .in3(not_2_out), .out(multiplexer_1_out), .sel(FS));  // open: en
  Multiplexer #(.select(2)) multiplexer_2 (
    .in0(1'b0), .in1(in_1[1]), .in2(xor_1_out), .in3(xor_2_out), .out(multiplexer_2_out), .sel(FS));  // open: en
  Multiplexer #(.select(2)) multiplexer_3 (
    .in0(1'b0), .in1(in_1[2]), .in2(xor_3_out), .in3(xor_4_out), .out(multiplexer_3_out), .sel(FS));  // open: en
  Multiplexer #(.select(2)) multiplexer_4 (
    .in0(1'b0), .in1(in_1[3]), .in2(xor_5_out), .in3(xor_6_out), .out(multiplexer_4_out), .sel(FS));  // open: en
  Multiplexer #(.select(2)) multiplexer_5 (
    .in0(1'b0), .in1(in_1[4]), .in2(xor_7_out), .in3(xor_8_out), .out(multiplexer_5_out), .sel(FS));  // open: en
  Multiplexer #(.select(2)) multiplexer_6 (
    .in0(1'b0), .in1(in_1[5]), .in2(xor_9_out), .in3(xor_10_out), .out(multiplexer_6_out), .sel(FS));  // open: en
  Multiplexer #(.select(2)) multiplexer_7 (
    .in0(1'b0), .in1(in_1[6]), .in2(xor_11_out), .in3(xor_12_out), .out(multiplexer_7_out), .sel(FS));  // open: en
  Multiplexer #(.select(2)) multiplexer_8 (
    .in0(1'b0), .in1(in_1[7]), .in2(xor_13_out), .in3(xor_14_out), .out(multiplexer_8_out), .sel(FS));  // open: en
  D_Flip_Flop d_ff_1 (.clk(CLOCK), .D(multiplexer_1_out), .Q(out_5[0]), .en(ENABLE));  // open: Qn, preset, reset
  D_Flip_Flop d_ff_2 (.clk(CLOCK), .D(multiplexer_2_out), .Q(out_5[1]), .en(ENABLE));  // open: Qn, preset, reset
  D_Flip_Flop d_ff_3 (.clk(CLOCK), .D(multiplexer_3_out), .Q(out_5[2]), .en(ENABLE));  // open: Qn, preset, reset
  D_Flip_Flop d_ff_4 (.clk(CLOCK), .D(multiplexer_4_out), .Q(out_5[3]), .en(ENABLE));  // open: Qn, preset, reset
  D_Flip_Flop d_ff_5 (.clk(CLOCK), .D(multiplexer_5_out), .Q(out_5[4]), .en(ENABLE));  // open: Qn, preset, reset
  D_Flip_Flop d_ff_6 (.clk(CLOCK), .D(multiplexer_6_out), .Q(out_5[5]), .en(ENABLE));  // open: Qn, preset, reset
  D_Flip_Flop d_ff_7 (.clk(CLOCK), .D(multiplexer_7_out), .Q(out_5[6]), .en(ENABLE));  // open: Qn, preset, reset
  D_Flip_Flop d_ff_8 (.clk(CLOCK), .D(multiplexer_8_out), .Q(out_5[7]), .en(ENABLE));  // open: Qn, preset, reset
  Hex_Digit_Display hex_digit_display_3 (.value(out_5[7:4]));  // open: dp
  Hex_Digit_Display hex_digit_display_4 (.value(out_5[3:0]));  // open: dp
endmodule

module alu (
  input  in_1,
  input  [7:0] A,
  input  [7:0] B,
  input  in_4,
  input  in_5,
  input  [3:0] FunSel,
  output [7:0] A_2
);

  wire adder_1_cout, and_1_out, not_1_out, not_2_out, not_3_out, not_4_out, not_5_out, not_6_out, not_7_out,
       not_8_out, not_9_out, not_10_out, not_11_out, not_12_out, not_13_out, not_14_out, not_15_out,
       not_16_out;
  wire [7:0] adder_1_out, and_2_out, or_1_out, subtractor_1_out, xor_1_out;

  Hex_Digit_Display hex_digit_display_1 (.value(A_2[7:4]));  // open: dp
  Hex_Digit_Display hex_digit_display_2 (.value(A_2[3:0]));  // open: dp
  not not_1 (not_1_out, B[0]);
  not not_2 (not_2_out, A[0]);
  Multiplexer #(.select(4), .enable("false")) multiplexer_1 (
    .in0(A[0]), .in1(B[0]), .in2(not_2_out), .in3(not_1_out), .in4(adder_1_out[0]), .in5(adder_1_out[0]),
    .in6(subtractor_1_out[0]), .in7(and_2_out[0]), .in8(or_1_out[0]), .in9(xor_1_out[0]), .in10(in_4),
    .in11(A[1]), .out(A_2[0]), .sel(FunSel));  // open: in12, in13, in14, in15
  not not_3 (not_3_out, B[1]);
  not not_4 (not_4_out, A[1]);
  Multiplexer #(.select(4), .enable("false")) multiplexer_2 (
    .in0(A[1]), .in1(B[1]), .in2(not_4_out), .in3(not_3_out), .in4(adder_1_out[1]), .in5(adder_1_out[1]),
    .in6(subtractor_1_out[1]), .in7(and_2_out[1]), .in8(or_1_out[1]), .in9(xor_1_out[1]), .in10(A[0]),
    .in11(A[2]), .out(A_2[1]), .sel(FunSel));  // open: in12, in13, in14, in15
  not not_5 (not_5_out, A[2]);
  not not_6 (not_6_out, B[2]);
  Multiplexer #(.select(4), .enable("false")) multiplexer_3 (
    .in0(A[2]), .in1(B[2]), .in2(not_5_out), .in3(not_6_out), .in4(adder_1_out[2]), .in5(adder_1_out[2]),
    .in6(subtractor_1_out[2]), .in7(and_2_out[2]), .in8(or_1_out[2]), .in9(xor_1_out[2]), .in10(A[1]),
    .in11(A[3]), .out(A_2[2]), .sel(FunSel));  // open: in12, in13, in14, in15
  and and_1 (and_1_out, FunSel[0], in_1);
  Adder adder_1 (.a(A), .b(B), .out(adder_1_out), .cin(and_1_out), .cout(adder_1_cout));
  Subtractor subtractor_1 (.a(A), .b(B), .out(subtractor_1_out));  // open: bin, bout
  assign {and_2_out[7], A[6], and_2_out[5:0]} = A & B;  // AND_Gate and_2, 8 bits wide
  assign or_1_out = A | B;  // OR_Gate or_1, 8 bits wide
  assign xor_1_out = A ^ B;  // XOR_Gate xor_1, 8 bits wide
  not not_7 (not_7_out, A[3]);
  not not_8 (not_8_out, B[3]);
  Multiplexer #(.select(4), .enable("false")) multiplexer_4 (
    .in0(A[3]), .in1(B[3]), .in2(not_7_out), .in3(not_8_out), .in4(adder_1_out[3]), .in5(adder_1_out[3]),
    .in6(subtractor_1_out[3]), .in7(and_2_out[3]), .in8(or_1_out[3]), .in9(xor_1_out[3]), .in10(A[2]),
    .in11(A[4]), .out(A_2[3]), .sel(FunSel));  // open: in12, in13, in14, in15
  not not_9 (not_9_out, A[4]);
  Hex_Digit_Display hex_digit_display_3 (.value(A[7:4]));  // open: dp
  Hex_Digit_Display hex_digit_display_4 (.value(A[3:0]));  // open: dp
  not not_10 (not_10_out, B[4]);
  Multiplexer #(.select(4), .enable("false")) multiplexer_5 (
    .in0(A[4]), .in1(B[4]), .in2(not_9_out), .in3(not_10_out), .in4(adder_1_out[4]), .in5(adder_1_out[4]),
    .in6(subtractor_1_out[4]), .in7(and_2_out[4]), .in8(or_1_out[4]), .in9(xor_1_out[4]), .in10(A[3]),
    .in11(A[5]), .out(A_2[4]), .sel(FunSel));  // open: in12, in13, in14, in15
  Hex_Digit_Display hex_digit_display_5 (.value(B[3:0]));  // open: dp
  Hex_Digit_Display hex_digit_display_6 (.value(B[7:4]));  // open: dp
  not not_11 (not_11_out, A[5]);
  not not_12 (not_12_out, B[5]);
  Multiplexer #(.select(4), .enable("false")) multiplexer_6 (
    .in0(A[5]), .in1(B[5]), .in2(not_11_out), .in3(not_12_out), .in4(adder_1_out[5]), .in5(adder_1_out[5]),
    .in6(subtractor_1_out[5]), .in7(and_2_out[5]), .in8(or_1_out[5]), .in9(xor_1_out[5]), .in10(A[4]),
    .in11(A[6]), .out(A_2[5]), .sel(FunSel));  // open: in12, in13, in14, in15
  not not_13 (not_13_out, B[6]);
  not not_14 (not_14_out, A[6]);
  Multiplexer #(.select(4), .enable("false")) multiplexer_7 (
    .in0(A[6]), .in1(B[6]), .in2(not_14_out), .in3(not_13_out), .in4(adder_1_out[6]), .in5(adder_1_out[6]),
    .in6(subtractor_1_out[6]), .in7(A[6]), .in8(or_1_out[6]), .in9(xor_1_out[6]), .in10(A[5]), .in11(A[7]),
    .out(A_2[6]), .sel(FunSel));  // open: in12, in13, in14, in15
  not not_15 (not_15_out, A[7]);
  not not_16 (not_16_out, B[7]);
  Multiplexer #(.select(4), .enable("false")) multiplexer_8 (
    .in0(A[7]), .in1(B[7]), .in2(not_15_out), .in3(not_16_out), .in4(adder_1_out[7]), .in5(adder_1_out[7]),
    .in6(subtractor_1_out[7]), .in7(and_2_out[7]), .in8(or_1_out[7]), .in9(xor_1_out[7]), .in10(A[6]),
    .in11(in_5), .out(A_2[7]), .sel(FunSel));  // open: in12, in13, in14, in15

  // Notes on the sheet:
  //   c register will come here
endmodule
