// Logisim project alu2.circ as structural Verilog: 3 circuits, main circuit main
module main (
  input  [3:0] FunSel,
  input  [7:0] A,
  input  [7:0] B,
  input  in_4,
  output [7:0] Out,
  output [3:0] ZCNO
);

  wire arithmetic_unit_1_carry_output, arithmetic_unit_1_overflow, shifter_1_carryout, shifter_1_overflow;
  wire [3:0] multiplexer_3_out;
  wire [7:0] and_1_out, arithmetic_unit_1_out, not_1_out, not_2_out, or_1_out, shifter_1_out, xor_1_out;

  arithmetic_unit arithmetic_unit_1 (
    .FunSel(FunSel[1:0]), .A(A), .B(B), .Carry(ZCNO[2]), .Out(arithmetic_unit_1_out),
    .Carry_output(arithmetic_unit_1_carry_output), .Overflow(arithmetic_unit_1_overflow));
  assign and_1_out = A & B;  // AND_Gate and_1, 8 bits wide
  assign or_1_out = A | B;  // OR_Gate or_1, 8 bits wide
  assign xor_1_out = A ^ B;  // XOR_Gate xor_1, 8 bits wide
  shifter shifter_1 (
    .Out(shifter_1_out), .CarryOut(shifter_1_carryout), .Funsel(FunSel[2:0]), .A(A),
    .Overflow(shifter_1_overflow));
  Multiplexer #(.enable("false")) multiplexer_1 (
    .in0(arithmetic_unit_1_carry_output), .in1(shifter_1_carryout), .out(multiplexer_3_out[2]),
    .sel(FunSel[3]));
  assign not_1_out = ~A;  // NOT_Gate not_1, 8 bits wide
  assign not_2_out = ~B;  // NOT_Gate not_2, 8 bits wide
  Multiplexer #(.select(4), .width(8), .enable("false")) multiplexer_2 (
    .in0(A), .in1(B), .in2(not_1_out), .in3(not_2_out), .in4(arithmetic_unit_1_out),
    .in5(arithmetic_unit_1_out), .in6(arithmetic_unit_1_out), .in7(and_1_out), .in8(or_1_out),
    .in9(xor_1_out), .in10(shifter_1_out), .in11(shifter_1_out), .in12(shifter_1_out), .in13(shifter_1_out),
    .in14(shifter_1_out), .in15(shifter_1_out), .out(Out), .sel(FunSel));
  nor nor_1 (multiplexer_3_out[3], Out[0], Out[1], Out[2], Out[3], Out[4], Out[5], Out[6]);
  Multiplexer #(.enable("false")) multiplexer_3 (
    .in0(arithmetic_unit_1_overflow), .in1(shifter_1_overflow), .out(multiplexer_3_out[0]), .sel(FunSel[3]));
  Register #(.width(4)) register_1 (
    .D({multiplexer_3_out[3:2], Out[7], multiplexer_3_out[0]}), .en(1'b1), .Q(ZCNO), .clk(in_4));  // open: clr
endmodule

// Arithmetic Unit
module arithmetic_unit (
  input  Carry,
  input  [1:0] FunSel,
  input  [7:0] A,
  input  [7:0] B,
  output [7:0] Out,
  output Carry_output,
  output Overflow
);

  wire and_1_out, multiplexer_1_out, multiplexer_2_out, xnor_1_out, xor_1_out, xor_2_out, xor_3_out;
  wire [7:0] adder_1_out, subtractor_1_out;

  and and_1 (and_1_out, Carry, FunSel[0]);
  xnor xnor_1 (xnor_1_out, B[7], A[7]);
  Adder adder_1 (.a(A), .b(B), .out(adder_1_out), .cin(and_1_out), .cout(Carry_output));
  Subtractor subtractor_1 (.a(A), .b(B), .out(subtractor_1_out));  // open: bin, bout
  xor xor_1 (xor_1_out, subtractor_1_out[7], A[7]);
  xor xor_2 (xor_2_out, adder_1_out[7], A[7]);
  xor xor_3 (xor_3_out, A[7], B[7]);
  Multiplexer #(.enable("false")) multiplexer_1 (
    .in0(1'b0), .in1(xor_2_out), .out(multiplexer_1_out), .sel(xnor_1_out));
  Multiplexer multiplexer_2 (.in0(1'b0), .in1(xor_1_out), .out(multiplexer_2_out), .sel(xor_3_out));  // open: en
  Multiplexer #(.select(2), .width(8), .enable("false")) multiplexer_3 (
    .in0(adder_1_out), .in1(adder_1_out), .in2(subtractor_1_out), .in3(subtractor_1_out), .out(Out),
    .sel(FunSel));
  Multiplexer #(.enable("false")) multiplexer_4 (
    .in0(multiplexer_1_out), .in1(multiplexer_2_out), .out(Overflow), .sel(FunSel[1]));

  // Notes on the sheet:
  //   Overflow output
endmodule

module shifter (
  input  [2:0] Funsel,
  input  [7:0] A,
  output [7:0] Out,
  output CarryOut,
  output Overflow
);

  wire xor_1_out, xor_2_out, xor_3_out;

  xor xor_1 (xor_1_out, A[6], A[7]);
  xor xor_2 (xor_2_out, A[0], A[7]);
  xor xor_3 (xor_3_out, A[7], A[6]);
  Multiplexer #(.select(3), .enable("false")) multiplexer_1 (
    .in0(1'b0), .in1(1'b0), .in2(1'b0), .in3(1'b0), .in4(xor_3_out), .in5(1'b0), .in6(xor_1_out),
    .in7(xor_2_out), .out(Overflow), .sel(Funsel));
  Multiplexer #(.select(3), .width(8), .enable("false")) multiplexer_2 (
    .in0({8{1'b0}}), .in1({8{1'b0}}), .in2({A[6:0], 1'b0}), .in3({1'b0, A[7:1]}), .in4({A[6:0], 1'b0}),
    .in5({{2{A[7]}}, A[6:1]}), .in6({A[6:0], A[7]}), .in7({A[0], A[7:1]}), .out(Out), .sel(Funsel));
  Multiplexer #(.select(3), .enable("false")) multiplexer_3 (
    .in0(1'b0), .in1(1'b0), .in2(A[7]), .in3(A[0]), .in4(1'b0), .in5(1'b0), .in6(A[7]), .in7(A[0]),
    .out(CarryOut), .sel(Funsel));

  // Notes on the sheet:
  //   Carry
endmodule
