// Logisim project part2.circ as structural Verilog: 1 circuit, main circuit main
module main (
  input  MuxCSel,
  input  [1:0] OutASel,
  input  [1:0] OutBSel,
  input  [1:0] FunSel,
  input  [3:0] RegSel,
  input  [1:0] MuxASel,
  input  [1:0] MuxBSel,
  input  [1:0] OutCSel,
  input  [1:0] OutDSel,
  input  [1:0] FunSel_2,
  input  [3:0] RegSel_2,
  input  L_H,
  input  Enable,
  input  [1:0] FunSel_3
);

  wire main_1_p1, main_1_p2, main_1_p3, n4_register_bank_1_p9;
  wire [1:0] n4_register_bank_1_p2;
  wire [7:0] main_1_p4, main_1_p8, main_2_p2, multiplexer_1_out, multiplexer_2_out, multiplexer_3_out,
       n3_register_bank_1_p6, n3_register_bank_1_p7, n4_register_bank_1_p8;
  wire [15:8] main_1_p8_2;

  Multiplexer #(.select(2), .width(8)) multiplexer_1 (
    .in0(main_1_p8), .in1(main_1_p4), .in2(n3_register_bank_1_p6), .in3(main_2_p2), .out(multiplexer_1_out),
    .sel(n4_register_bank_1_p2));  // open: en
  // _4_register_bank 4_register_bank_1: pin names not known; wires that end beside it: MuxASel, n4_register_bank_1_p2, RegSel, multiplexer_1_out, FunSel, OutASel, OutBSel, n4_register_bank_1_p8, n4_register_bank_1_p9, n4_register_bank_1_p9
  Multiplexer #(.select(2), .width(8)) multiplexer_2 (
    .in1(main_1_p8), .in2(main_1_p4), .in3(main_2_p2), .out(multiplexer_2_out), .sel(MuxBSel));  // open: in0, en
  // _2c_main main_1: pin names not known; wires that end beside it: main_1_p1, main_1_p2, main_1_p3, main_1_p4, main_1_p1, main_1_p3, main_1_p2, {main_1_p8_2, main_1_p8}
  Multiplexer #(.width(8)) multiplexer_3 (
    .in0(multiplexer_1_out), .in1(n4_register_bank_1_p8), .out(multiplexer_3_out), .sel(MuxCSel));  // open: en
  // alu2_main main_2: pin names not known; wires that end beside it: multiplexer_3_out, main_2_p2
  // _3_register_bank 3_register_bank_1: pin names not known; wires that end beside it: RegSel_2, multiplexer_2_out, FunSel_2, OutCSel, OutDSel, n3_register_bank_1_p6, n3_register_bank_1_p7
  Register register_1 (.D(n3_register_bank_1_p7), .Q(main_1_p4));  // open: en, clk, clr

  // Notes on the sheet:
  //   A
  //   B
  //   Bu kısım eklenecek
  //   C
  //   Bu kısımdan çok emin değil
  //   Bi de sen bak
endmodule
